# Fritzing sketch projeto_firtzing (saved by Fritzing 0.9.3b)
breadboards: 1

parts:
  U1 = ESP8266 NodeMCU LoLin module
  KF-1 = KF-301 Relay [package=THT]
  KF-2 = KF-301 Relay [package=THT]
  KF-3 = KF-301 Relay [package=THT]
  KF-4 = KF-301 Relay [package=THT]
  Mod1 = KY-015 Temperature & Humidity Sensor Module [package="Breakout board"]
  VALVE1 = Plastic Solenoid Valve
  VALVE2 = Plastic Solenoid Valve
  VALVE3 = Plastic Solenoid Valve
  VALVE4 = Plastic Solenoid Valve
  Componente1 = Soil Moisture Sensor
  U2 = LIPO-1000mAh [package=lipo-1000]

nets:
  N1: U1.D0, Mod1.S
  N2: U1.D1, KF-2.signal
  N3: U1.D2, KF-3.signal
  N4: U1.D3, KF-4.signal
  N5: U1.D4, KF-1.signal
  N6: U1.D8, Componente1.SIG
  3V3: U1.3V3, KF-1.power, KF-2.power, KF-3.power, KF-4.power, Mod1.Vin, Componente1.VCC
  N7: U1.Vin, U2.+
  GND: U1.GND, KF-1.ground, KF-2.ground, KF-3.ground, KF-4.ground, Mod1.-, Componente1.GND, U2.-
  N8: KF-1.C, VALVE1.no_name_yet#1
  N9: KF-1.NO, VALVE1.no_name_yet#2
  N10: KF-2.C, VALVE2.no_name_yet#1
  N11: KF-2.NO, VALVE2.no_name_yet#2
  N12: KF-3.C, VALVE3.no_name_yet#2
  N13: KF-3.NO, VALVE3.no_name_yet#1
  N14: KF-4.C, VALVE4.no_name_yet#1
  N15: KF-4.NO, VALVE4.no_name_yet#2

notes:
  Solenoides de fluxo da água
  Porjeto horta 4.0 SESI-SENAI-AP esquema de ligação.
  Sensor de solo
  Sensor de temp. e Umid.
  Esp8266
  Relés
  Bateria

custom parts:
  ESP8266 NodeMCU LoLin module: ESP8266 based NodeMCU
  KF-301 Relay: KF-301
  KY-015 Temperature & Humidity Sensor Module: KY-015 temperature and humidity sensor module, provides a low-latency serial interface to measure humidity and temperature.
